# Fritzing sketch Login_Test_Diagram (saved by Fritzing 0.9.9b)
breadboards: 1

parts:
  Arduino = Arduino Uno (Rev3)
  Rotary_Encoder = mystery part, 5 pins [chip_label=?]
  S1 = Pushbutton [package="[SMD]"]

nets:
  N1: Arduino.D2, Arduino.GND, Rotary_Encoder.pin5, S1.Pin_3, S1.Pin_4
  N2: Arduino.D3_PWM, Rotary_Encoder.pin3
  N3: Arduino.D6_PWM, Rotary_Encoder.pin2
  N4: Arduino.D7, Rotary_Encoder.pin1
  N5: Arduino.5V, Rotary_Encoder.pin4
